# Fritzing sketch altimetro (saved by Fritzing 0.9.10b)

parts:
  Part1 = Arduino Pro Mini (5V)
  Part2 = Barometric Pressure Sensor - BMP180 Breakout (GY-68)
  LED1 = smd LED [color="Red (633nm)" package="0805 [SMD]"]
  R1 = Resistor [tolerance=±5% resistance=220 package="0805 [SMD]"]

nets:
  N1: Part1.A4, Part2.SDA
  N2: Part1.A5, Part2.SCL
  GND: Part1.GND, Part2.GND, LED1.cathode
  VCC: Part1.VCC, Part2.VCC
  N3: Part1.SCK, R1.Pin_1
